// Logisim project CustomMultiplier.circ as structural Verilog: 1 circuit, main circuit CustomMultiplier
module CustomMultiplier (
  input  [7:0] FirstOperand,
  input  [7:0] SecondOperand,
  input  Clock,
  output [7:0] Result,
  output Done
);

  wire comparator_1_eq, comparator_2_eq, d_ff_1_q, not_1_out, not_2_out, or_1_out;
  wire [7:0] counter_1_q, multiplexer_1_out, register_1_q;

  not not_1 (not_1_out, Done);
  Multiplexer #(.width(8)) multiplexer_1 (.in0({8{1'b0}}), .in1(register_1_q), .out(multiplexer_1_out), .sel(d_ff_1_q));
  D_Flip_Flop d_ff_1 (.D(or_1_out), .clk(Clock), .Q(d_ff_1_q));  // open: Qn, preset, reset
  Counter counter_1 (
    .clr(1'b0), .load(1'b0), .up(1'b1), .count(not_1_out), .clk(Clock), .Q(counter_1_q));  // open: D, carry
  or or_1 (or_1_out, register_1_q[0], register_1_q[1], register_1_q[2], register_1_q[3], register_1_q[4], register_1_q[5], register_1_q[6], register_1_q[7]);
  CustomAdder customadder_1 (.FirstOperand(FirstOperand), .SecondOperand(multiplexer_1_out), .Result(Result));
  not not_2 (not_2_out, Done);
  Register register_1 (.D(Result), .en(not_2_out), .clk(Clock), .Q(register_1_q));  // open: clr
  Comparator comparator_1 (.a(SecondOperand), .b(counter_1_q), .eq(comparator_1_eq));  // open: gt, lt
  Comparator comparator_2 (.a(SecondOperand), .b(8'h1), .eq(comparator_2_eq));  // open: gt, lt
  or or_2 (Done, comparator_1_eq, comparator_2_eq);

  // Other names for the same wires on the sheet: A[7:0] = FirstOperand; B[7:0] = SecondOperand; C[7:0] = Result;
  //   clk = Clock
endmodule
